# Fritzing sketch wiring (saved by Fritzing 0.9.3b)

parts:
  M1 = >Wemos D1 R32
  SHT_30 = SHT3X [form="♂ (male)" package=THT]  # not connected
  MH-Z19B = MH-Z19C
  BH1750 = BH1750 [form="♂ (male)" package=THT]  # not connected
  Relay_5v = Keyes Relay [package=THT]
  D1 = Rectifier Diode [part_number=1N4001 package="300 mil [THT]"]
  TIP41C = Basic FET P-Channel [package="TO220 [THT]"]
  NPN_2N222 = LM35 Temperature Sensor [package="TO92 [THT]"]
  TIP41C_2 = Basic FET P-Channel [package="TO220 [THT]"]
  51_ohm = Resistor [tolerance=±5% resistance=220 package="1206 [SMD]"]
  RTC_DS3231 = ZS-042 RTC Module
  dioda_flyback = Rectifier Diode [part_number=1N4001 package="300 mil [THT]"]
  51_ohm_2 = Resistor [tolerance=±5% resistance=220 package="1206 [SMD]"]
  lampu = 2.1mm Barrel Jack with Terminal Block
  Mist_maker = 2.1mm Barrel Jack with Terminal Block
  Power_supply = 2.1mm Barrel Jack with Terminal Block
  power_supply = 2.1mm Barrel Jack with Terminal Block
  power_supply_2 = 2.1mm Barrel Jack with Terminal Block
  solenoid = 2.1mm Barrel Jack with Terminal Block
  dioda_flyback_2 = Rectifier Diode [part_number=1N4001 package="300 mil [THT]"]  # not connected
  D2 = Rectifier Diode [part_number=1N4001 package="300 mil [THT]"]  # not connected
  dioda_flyback_3 = Rectifier Diode [part_number=1N4001 package="300 mil [THT]"]  # not connected

nets:
  5V: M1.5V, MH-Z19B.Vin, Relay_5v.power, dioda_flyback.cathode
  3V3: M1.3V3, RTC_DS3231.VCC
  GND: M1.GND, MH-Z19B.GND, D1.anode, NPN_2N222.+Vs, RTC_DS3231.GND, power_supply_2.POS
  N1: M1.RX0, MH-Z19B.Rx
  N2: M1.TX0, MH-Z19B.Tx
  N3: M1.IO12, 51_ohm_2.Pin_1
  N4: M1.IO13, 51_ohm.Pin_1
  N5: M1.IO5, NPN_2N222.Vout
  N6: M1.SDA, RTC_DS3231.SDA
  N7: M1.SCL, RTC_DS3231.SCL
  N8: Relay_5v.ground, NPN_2N222.GND, dioda_flyback.anode
  N9: Relay_5v.C, power_supply.POS
  N10: Relay_5v.NO, lampu.POS
  N11: TIP41C.source, Mist_maker.NEG
  N12: TIP41C_2.drain, Power_supply.NEG
  N13: TIP41C_2.source, solenoid.NEG
  N14: lampu.NEG, power_supply.NEG
  N15: Mist_maker.POS, power_supply_2.NEG
  N16: Power_supply.POS, solenoid.POS

custom parts:
  >Wemos D1 R32: Wemos D1 R32 - This board is used with dual-mode Wi-Fi and Bluetooth chips, which is safe, reliable, and scalable to a variety of applications. DC in 5V-12V, 1 analog input(3.2V max input), a Micro USB connection, Compatible with D1 R32=WiFi+bluetooth+UNO
  SHT3X: SHT31 SHT31-D Temperature & Humidity Sensor Breakout
  MH-Z19C: CO2-Sensor https://www.winsen-sensor.com/
  BH1750: BH1750FVI is an digital Ambient Light Sensor IC for I2 C bus interface. This IC is the most suitable to obtain the ambient light data for adjusting LCD and Keypad backlight power of Mobile phone. It is possible to detect wide range at High resolution.
  Keyes Relay: The Keyes 5V relay module is suitable for SCM development, home appliance control. It uses a 5V~12V TIL control signal which can control DC / AC signal.
